# Fritzing sketch Untitled Sketch 2 (saved by Fritzing 0.9.3b)
breadboards: 1

parts:
  Tiva_C_LaunchPad1 = Tiva C TM4C123G [package=THT]
  T1 = LM35 Temperature Sensor [package="TO92 [THT]"]
  J1 = Piezo Speaker
  U1 = Module 4 Relais 5V [package="Module 4 Relais 5V"]
  BULB1 = Incandescent light bulb small [package="bulb sm"]
  JL012-13-5_1 = JL012-13-5.2 Lever (Limit) Switch SPDT + NO + NC [part_number=JL012-13-5.2]
  JL012-13-5_2 = JL012-13-5.2 Lever (Limit) Switch SPDT + NO + NC [part_number=JL012-13-5.2]

nets:
  N1: Tiva_C_LaunchPad1.PB0, JL012-13-5_1.NO
  N2: Tiva_C_LaunchPad1.PD0, JL012-13-5_2.NO
  N3: Tiva_C_LaunchPad1.PE3, T1.Vout
  N4: Tiva_C_LaunchPad1.PF1, J1.pin2
  N5: Tiva_C_LaunchPad1.PF2, U1.IN1
  GND: Tiva_C_LaunchPad1.GND, T1.GND, J1.pin1, U1.GND, JL012-13-5_1.C, JL012-13-5_2.C
  N6: Tiva_C_LaunchPad1.PB2, U1.IN2
  N7: U1.K1-NF, BULB1.1

custom parts:
  Tiva C TM4C123G: Tiva C LaunchPad EK-TM4C123GXL
  Module 4 Relais 5V: Module 4 Relais 5V 4x SPD-06VDC-SD-C
  JL012-13-5.2 Lever (Limit) Switch SPDT + NO + NC: Micro Switch; Model No.: JL012-13.5-2; Actuator Action: Momentary; Actuator Type: Hinge Lever; Contact Configuration: 1NO, 1NC (SPDT) Temperature -25~65℃；Relative humidity: below 85%; Rate Voltage: 125V AC; Rated Current: 1A.
